# Fritzing sketch servo (saved by Fritzing 0.9.3b)
breadboards: 1

parts:
  Componente1 = Arduino Uno (Rev3)
  J1 = Basic Servo [part_number=servo]

nets:
  N1: Componente1.D6_PWM, J1.pulse
  5V: Componente1.5V, J1.vcc
  GND: Componente1.GND, J1.gnd
